// Logisim project t11-2.circ as structural Verilog: 1 circuit, main circuit main
module main (
  input  A,
  input  B,
  input  C,
  input  D
);

  wire and_1_out, and_2_out, and_3_out, and_4_out, and_5_out, and_6_out, and_7_out, and_8_out, and_9_out,
       not_1_out, not_2_out, not_3_out, not_4_out, not_5_out, not_6_out, not_7_out, not_8_out, not_9_out,
       or_1_out, or_2_out, or_3_out, or_4_out, or_5_out;

  and and_1 (and_1_out, A, B);
  not not_1 (not_1_out, C);
  and and_2 (and_2_out, A, B);
  not not_2 (not_2_out, C);
  and and_3 (and_3_out, not_2_out, D);
  or or_1 (or_1_out, A, B);
  not not_3 (not_3_out, C);
  not not_4 (not_4_out, D);
  not not_5 (not_5_out, A);
  not not_6 (not_6_out, B);
  not not_7 (not_7_out, D);
  or or_2 (or_2_out, not_1_out, D);
  and and_4 (and_4_out, and_2_out, and_3_out);
  or or_3 (or_3_out, not_3_out, not_4_out);
  and and_5 (and_5_out, not_5_out, not_6_out);
  and and_6 (and_6_out, C, not_7_out);
  not not_8 (not_8_out, and_7_out);
  and and_7 (and_7_out, and_1_out, or_2_out);
  or or_4 (or_4_out, or_1_out, or_3_out);
  and and_8 (and_8_out, and_5_out, and_6_out);
  not not_9 (not_9_out, and_8_out);
  and and_9 (and_9_out, not_8_out, and_4_out);
  or or_5 (or_5_out, or_4_out, not_9_out);
  // AND_Gate and_10 has open pins: in0=and_9_out, in4=or_5_out, out=open
endmodule
