// Logisim project t11-exerc3.circ as structural Verilog: 1 circuit, main circuit main
module main (
  input  A,
  input  B,
  input  C,
  input  D,
  input  A_2,
  input  B_2,
  input  C_2,
  input  A_3,
  input  B_3,
  input  C_3,
  input  A_4,
  input  B_4,
  input  C_4
);

  wire and_1_out, and_2_out, and_3_out, and_4_out, and_5_out, and_6_out, and_7_out, and_8_out, and_9_out,
       and_10_out, and_11_out, and_12_out, nand_1_out, nand_2_out, not_1_out, not_2_out, not_3_out,
       not_4_out, not_5_out, not_6_out, not_7_out, not_8_out, not_9_out, not_10_out, not_11_out, not_12_out,
       not_13_out, or_1_out, or_2_out, or_3_out, or_4_out, or_5_out, or_6_out, or_7_out, or_8_out, or_9_out,
       or_10_out;

  not not_1 (not_1_out, A_2);
  not not_2 (not_2_out, C_2);
  not not_3 (not_3_out, A_3);
  not not_4 (not_4_out, A_3);
  and and_1 (and_1_out, not_1_out, B_2);
  and and_2 (and_2_out, A_2, not_2_out);
  nand nand_1 (nand_1_out, A_2, B_2, C_2);
  or or_1 (or_1_out, not_3_out, not_4_out);
  or or_2 (or_2_out, A_3, A_3);
  or or_3 (or_3_out, and_1_out, and_2_out);
  or or_4 (or_4_out, A_2, nand_1_out);
  buf and_3 (and_3_out, or_1_out);  // AND_Gate
  and and_4 (and_4_out, or_2_out, A_3);
  or or_5 (or_5_out, or_3_out, or_4_out);
  and and_5 (and_5_out, and_3_out, and_4_out);
  not not_5 (not_5_out, B);
  not not_6 (not_6_out, A);
  not not_7 (not_7_out, D);
  and and_6 (and_6_out, A_4, B_4);
  not not_8 (not_8_out, A_4);
  not not_9 (not_9_out, B_4);
  not not_10 (not_10_out, A_4);
  not not_11 (not_11_out, C_4);
  and and_7 (and_7_out, A, not_5_out);
  and and_8 (and_8_out, not_6_out, B);
  nand nand_2 (nand_2_out, A, C);
  and and_9 (and_9_out, A, not_7_out);
  and and_10 (and_10_out, A, B, C, D);
  or or_6 (or_6_out, not_8_out, not_9_out);
  and and_11 (and_11_out, not_10_out, B_4, not_11_out);
  and and_12 (and_12_out, and_7_out, C);
  or or_7 (or_7_out, nand_2_out, and_9_out);
  not not_12 (not_12_out, or_6_out);
  not not_13 (not_13_out, and_11_out);
  or or_8 (or_8_out, and_12_out, and_8_out);
  or or_9 (or_9_out, and_6_out, not_12_out);
  or or_10 (or_10_out, or_8_out, or_7_out);
  // OR_Gate or_11 has open pins: in0=or_9_out, in3=not_13_out, out=open
  // OR_Gate or_12 has open pins: in1=or_10_out, in3=and_10_out, out=open

  assign B_3 = A_3;
  assign C_3 = A_3;

  // Notes on the sheet:
  //   Exerc 3 / a)
  //   Exerc 3 / b)
  //   S
  //   S
  //   Exerc 3 / c)
  //   Exerc 3 / d)
endmodule
