// Logisim project Questao4.circ as structural Verilog: 3 circuits, main circuit main
module main (
  input  in_1,
  input  in_2,
  input  in_3,
  input  in_4,
  input  in_5,
  input  in_6,
  input  in_7,
  input  PARIDADE,
  input  a,
  input  b,
  input  c,
  input  PARIDADE_2,
  output ERRO,
  output x
);

  wire and_1_out, and_2_out, and_3_out, and_4_out, not_1_out, not_2_out, not_3_out, not_4_out, not_5_out,
       not_6_out, or_1_out, undriven;

  Decoder #(.select(3)) decoder_1 (
    .out0(in_1), .out1(in_2), .out2(in_3), .out3(in_4), .out4(in_5), .out5(in_6), .out6(in_7), .en(undriven));  // open: out7, sel
  not not_1 (not_1_out, a);
  and and_1 (and_1_out, not_1_out, not_2_out, c);
  not not_2 (not_2_out, b);
  not not_3 (not_3_out, a);
  and and_2 (and_2_out, not_3_out, b, not_4_out);
  not not_4 (not_4_out, c);
  and and_3 (and_3_out, a, not_5_out, not_6_out);
  not not_5 (not_5_out, b);
  not not_6 (not_6_out, c);
  and and_4 (and_4_out, a, b, c);
  or or_1 (or_1_out, and_1_out, and_2_out, and_3_out, and_4_out);
  LED led_1 (.in(ERRO));
  and and_5 (ERRO, undriven, PARIDADE);
  and and_6 (x, or_1_out, PARIDADE_2);
  LED led_2 (.in(x));

  // Notes on the sheet:
  //   Quest 4 Simplificada 
  //   Quest 4
endmodule

module quest_4_1 (
  input  in_1,
  input  in_2,
  input  in_3,
  input  in_4,
  input  in_5,
  input  in_6,
  input  in_7,
  input  in_8,
  output out_9
);
endmodule

module teste_karnaguh (
  input  a,
  input  b,
  input  c,
  input  PARIDADE,
  output x
);

  wire and_1_out, and_2_out, and_3_out, and_4_out, not_1_out, not_2_out, not_3_out, not_4_out, not_5_out,
       not_6_out, or_1_out;

  not not_1 (not_1_out, a);
  not not_2 (not_2_out, b);
  not not_3 (not_3_out, a);
  not not_4 (not_4_out, c);
  not not_5 (not_5_out, b);
  not not_6 (not_6_out, c);
  and and_1 (and_1_out, not_1_out, not_2_out, c);
  and and_2 (and_2_out, not_3_out, b, not_4_out);
  and and_3 (and_3_out, a, not_5_out, not_6_out);
  and and_4 (and_4_out, a, b, c);
  or or_1 (or_1_out, and_1_out, and_2_out, and_3_out, and_4_out);
  and and_5 (x, or_1_out, PARIDADE);
  LED led_1 (.in(x));
endmodule
