// Logisim project quest_4.circ as structural Verilog: 1 circuit, main circuit main
module main (
  input  in_1,
  input  in_2,
  input  in_3,
  input  in_4,
  input  in_5,
  input  in_6,
  input  in_7,
  input  in_8
);

  wire or_1_out, undriven, undriven_2;

  Decoder #(.select(2)) decoder_1 (.out0(in_1), .out1(in_2), .out2(in_3), .out3(in_4), .en(undriven));  // open: sel
  Decoder #(.select(2)) decoder_2 (.out0(in_5), .out1(in_6), .out2(in_7), .out3(in_8), .en(undriven_2));  // open: sel
  LED led_1 (.in(or_1_out));
  or or_1 (or_1_out, undriven, undriven_2);

  // Notes on the sheet:
  //   T15 - QUESTÃO 4
endmodule
