// Logisim project T16 Decodificador 4x16.circ as structural Verilog: 1 circuit, main circuit main
module main (
  input  H,
  input  E0,
  input  E1,
  input  E2,
  input  E3,
  output D8,
  output D9,
  output D10,
  output D11,
  output D12,
  output D13,
  output D14,
  output D15,
  output D0,
  output D1,
  output D2,
  output D3,
  output D4,
  output D5,
  output D6,
  output D7
);

  wire not_1_out, not_2_out, not_3_out, not_4_out;

  not not_1 (not_1_out, E0);
  not not_2 (not_2_out, E1);
  not not_3 (not_3_out, E2);
  not not_4 (not_4_out, E3);
  and u_D8 (D8, E3, not_3_out, H, not_2_out, not_1_out);
  and u_D0 (D0, not_4_out, not_3_out, H, not_2_out, not_1_out);
  and u_D9 (D9, E3, not_3_out, H, not_2_out, E0);
  and u_D10 (D10, E3, not_3_out, H, E1, not_1_out);
  and u_D1 (D1, not_4_out, not_3_out, H, not_2_out, E0);
  and u_D2 (D2, not_4_out, not_3_out, H, E1, not_1_out);
  and u_D11 (D11, E3, not_3_out, H, E1, E0);
  and u_D3 (D3, not_4_out, not_3_out, H, E1, E0);
  and u_D12 (D12, E3, E2, H, not_2_out, not_1_out);
  and u_D4 (D4, not_4_out, E2, H, not_2_out, not_1_out);
  and u_D13 (D13, E3, E2, H, not_2_out, E0);
  and u_D5 (D5, not_4_out, E2, H, not_2_out, E0);
  and u_D14 (D14, E3, E2, H, E1, not_1_out);
  and u_D6 (D6, not_4_out, E2, H, E1, not_1_out);
  and u_D15 (D15, E3, E2, H, E1, E0);
  and u_D7 (D7, not_4_out, E2, H, E1, E0);
endmodule
