// Logisim project T16 Demultiplexador 8x3.circ as structural Verilog: 1 circuit, main circuit main
module main (
  input  E0,
  input  A2,
  input  A1,
  input  A0,
  output S0,
  output S1,
  output S2,
  output S3,
  output S4,
  output S5,
  output S6,
  output S7
);

  wire not_1_out, not_2_out, not_3_out, not_4_out, not_5_out, not_6_out, not_7_out, not_8_out, not_9_out,
       not_10_out, not_11_out, not_12_out;

  not not_1 (not_1_out, A2);
  not not_2 (not_2_out, A1);
  not not_3 (not_3_out, A0);
  not not_4 (not_4_out, A2);
  not not_5 (not_5_out, A1);
  not not_6 (not_6_out, A2);
  not not_7 (not_7_out, A0);
  not not_8 (not_8_out, A2);
  not not_9 (not_9_out, A1);
  not not_10 (not_10_out, A0);
  not not_11 (not_11_out, A1);
  not not_12 (not_12_out, A0);
  and and_1 (S0, not_1_out, not_2_out, not_3_out, E0);
  and and_2 (S1, not_4_out, not_5_out, A0, E0);
  and and_3 (S2, not_6_out, A1, not_7_out, E0);
  and and_4 (S3, not_8_out, A1, A0, E0);
  and and_5 (S4, A2, not_9_out, not_10_out, E0);
  and and_6 (S5, A2, not_11_out, A0, E0);
  and and_7 (S6, A2, A1, not_12_out, E0);
  and and_8 (S7, A2, A1, A0, E0);
endmodule
