// Logisim project T16 Multiplexador 3x8.circ as structural Verilog: 1 circuit, main circuit main
module main (
  input  E0,
  input  E1,
  input  E2,
  input  E3,
  input  E4,
  input  E5,
  input  E6,
  input  E7,
  input  A2,
  input  A1,
  input  A0,
  output \Saída 
);

  wire and_1_out, and_2_out, and_3_out, and_4_out, and_5_out, and_6_out, and_7_out, and_8_out, not_1_out,
       not_2_out, not_3_out, not_4_out, not_5_out, not_6_out, not_7_out, not_8_out, not_9_out, not_10_out,
       not_11_out, not_12_out;

  not not_1 (not_1_out, A2);
  not not_2 (not_2_out, A1);
  not not_3 (not_3_out, A0);
  not not_4 (not_4_out, A2);
  not not_5 (not_5_out, A1);
  not not_6 (not_6_out, A2);
  not not_7 (not_7_out, A0);
  not not_8 (not_8_out, A2);
  not not_9 (not_9_out, A1);
  not not_10 (not_10_out, A0);
  not not_11 (not_11_out, A1);
  not not_12 (not_12_out, A0);
  and and_1 (and_1_out, not_1_out, not_2_out, not_3_out, E0);
  and and_2 (and_2_out, not_4_out, not_5_out, A0, E1);
  and and_3 (and_3_out, not_6_out, A1, not_7_out, E2);
  and and_4 (and_4_out, not_8_out, A1, A0, E3);
  and and_5 (and_5_out, A2, not_9_out, not_10_out, E4);
  and and_6 (and_6_out, A2, not_11_out, A0, E5);
  and and_7 (and_7_out, A2, A1, not_12_out, E6);
  and and_8 (and_8_out, A2, A1, A0, E7);
  or or_1 (\Saída , and_1_out, and_2_out, and_3_out, and_4_out, and_5_out, and_6_out, and_7_out, and_8_out);
endmodule
