// Logisim project soma2bits.circ as structural Verilog: 2 circuits, main circuit Somador Completo
// FA
module Somador_Completo (
  input  A,
  input  B,
  input  Cin,
  output S,
  output Cout
);

  wire and_1_out, and_2_out, and_3_out;

  xor xor_1 (S, A, Cin, B);
  and and_1 (and_1_out, A, Cin);
  and and_2 (and_2_out, A, B);
  and and_3 (and_3_out, B, Cin);
  or or_1 (Cout, and_1_out, and_2_out, and_3_out);

  // Notes on the sheet:
  //   FA - Um somandor completo feito com portas lógicas
  //   Um XOR com mais de duas portas precisa ser configurado
  //   no logisim para funcionar. Deve-se mudar para
  //   "Quando existir um número impar"
endmodule

module Soma2bis (
  input  A1,
  input  A0,
  input  B1,
  input  B0,
  input  Soma,
  output S1,
  output S0,
  output Count
);

  wire somador_completo_1_cout, xor_1_out, xor_2_out;

  xor xor_1 (xor_1_out, B1, Soma);
  xor xor_2 (xor_2_out, Soma, B0);
  Somador_Completo somador_completo_1 (.A(A0), .B(xor_2_out), .Cin(Soma), .S(S0), .Cout(somador_completo_1_cout));
  Somador_Completo somador_completo_2 (.A(A1), .B(xor_1_out), .Cin(somador_completo_1_cout), .S(S1), .Cout(Count));

  // Notes on the sheet:
  //   0==soma, 1==diminui
  //   Se soma for um, o XOR acaba atuando como um NOT
  //   invertendo os bits de B0 e B1 (complementando o B)
endmodule
