// Logisim project t21_Fsomador.circ as structural Verilog: 3 circuits, main circuit main
module main (
  input  [7:0] in_1,
  input  in_2,
  output _8,
  output _4,
  output _2,
  output _1
);

  Full_Soma full_soma_1 (.So_Su(in_2), .A(in_1[7:4]), .B(in_1[3:0]), .S1(_2), .S0(_1), .S3(_8), .S2(_4));
endmodule

// FA
module soma (
  input  A,
  input  B,
  input  Cin,
  output S,
  output Cout
);

  wire and_1_out, and_2_out, and_3_out, xor_1_out;

  xor xor_1 (xor_1_out, A, B);
  and and_1 (and_1_out, A, B);
  and and_2 (and_2_out, A, Cin);
  and and_3 (and_3_out, B, Cin);
  or or_1 (Cout, and_1_out, and_2_out, and_3_out);
  xor xor_2 (S, xor_1_out, Cin);
endmodule

module Full_Soma (
  input  [3:0] A,
  input  [3:0] B,
  input  So_Su,
  output S3,
  output S2,
  output S1,
  output S0
);

  wire soma_1_cout, soma_2_cout, soma_3_cout, xor_1_out, xor_2_out, xor_3_out, xor_4_out;

  soma soma_1 (.A(A[0]), .B(xor_1_out), .Cin(So_Su), .S(S0), .Cout(soma_1_cout));
  xor xor_1 (xor_1_out, So_Su, B[0]);
  xor xor_2 (xor_2_out, So_Su, B[1]);
  soma soma_2 (.A(A[1]), .B(xor_2_out), .Cin(soma_1_cout), .S(S1), .Cout(soma_2_cout));
  xor xor_3 (xor_3_out, So_Su, B[2]);
  soma soma_3 (.A(A[2]), .B(xor_3_out), .Cin(soma_2_cout), .S(S2), .Cout(soma_3_cout));
  xor xor_4 (xor_4_out, So_Su, B[3]);
  soma soma_4 (.A(A[3]), .B(xor_4_out), .Cin(soma_3_cout), .S(S3));  // open: Cout

  // Other names for the same wires on the sheet: Aa = A[0]; Ab = A[1]; Ac = A[2]; Ad = A[3]; Ba = B[0]; Bb = B[1];
  //   Bc = B[2]; Bd = B[3]
endmodule
