// Logisim project flips-flops.circ as structural Verilog
module latche (
  input  Reset,
  input  Set,
  output Q,
  output Q_prime
);

  nor nor_1 (Q, Reset, Q_prime);
  nor nor_2 (Q_prime, Q, Set);

  // Notes on the sheet:
  //   Circuito Sequêncial (latche - Início de uma memória)
endmodule

module Somador (
  input  A,
  input  B,
  input  Cin,
  output \Saída ,
  output Cout
);

  wire and_1_out, and_2_out, and_3_out;

  ExactlyOne xor_1 (.out(\Saída ), .in0(A), .in1(B), .in2(Cin));
  and and_1 (and_1_out, A, B);
  or or_1 (Cout, and_1_out, and_2_out, and_3_out);
  and and_2 (and_2_out, A, Cin);
  and and_3 (and_3_out, B, Cin);

  // Notes on the sheet:
  //   Circuito Combinacional (Somador de 1bit)
endmodule

module Flip_FLop_JK (
  input  K,
  input  Habilita,
  input  J,
  output Q,
  output Q_prime
);

  wire and_1_out, and_2_out, and_3_out, and_4_out;

  and and_1 (and_1_out, K, Q);
  and and_2 (and_2_out, Q_prime, J);
  and and_3 (and_3_out, and_1_out, Habilita);
  and and_4 (and_4_out, Habilita, and_2_out);
  nor nor_1 (Q, and_3_out, Q_prime);
  nor nor_2 (Q_prime, Q, and_4_out);

  // Notes on the sheet:
  //   Tipo T
  //   Flip-Flop tipo JK (tipo D + Tipo T)
  //   Tipo D
endmodule
