// Logisim project q4.circ as structural Verilog: 2 circuits, main circuit main
module main (
  input  in_1,
  input  in_2
);

  wire button_1_out, clock_1_out, clock_2_out;
  wire [3:0] ff_t_1_q, not_1_out, not_2_out, t_ff_1_q;

  Clock clock_1 (.out(clock_1_out));
  Flip_Flop_T ff_t_1 (.Clock(clock_1_out), .Entrada(in_1), .Q(ff_t_1_q[0]));  // open: Q_prime
  Flip_Flop_T ff_t_2 (.Clock(ff_t_1_q[0]), .Entrada(in_1), .Q(ff_t_1_q[1]));  // open: Q_prime
  Flip_Flop_T ff_t_3 (.Clock(ff_t_1_q[1]), .Entrada(in_1), .Q(ff_t_1_q[2]));  // open: Q_prime
  Flip_Flop_T ff_t_4 (.Clock(ff_t_1_q[2]), .Entrada(in_1), .Q(ff_t_1_q[3]));  // open: Q_prime
  Hex_Digit_Display hex_digit_display_1 (.value(not_1_out));  // open: dp
  assign not_1_out = ~ff_t_1_q;  // NOT_Gate not_1, 4 bits wide
  Clock clock_2 (.out(clock_2_out));
  // NAND_Gate nand_1 has open pins: in0=in_2, in1=in_2, out=open
  Button button_1 (.out(button_1_out));
  T_Flip_Flop t_ff_1 (.clk(clock_2_out), .T(in_2), .Q(t_ff_1_q[0]), .preset(button_1_out));  // open: Qn, reset, en
  T_Flip_Flop t_ff_2 (.clk(t_ff_1_q[0]), .T(in_2), .Q(t_ff_1_q[1]), .preset(button_1_out));  // open: Qn, reset, en
  T_Flip_Flop t_ff_3 (.clk(t_ff_1_q[1]), .T(in_2), .Q(t_ff_1_q[2]), .preset(button_1_out));  // open: Qn, reset, en
  T_Flip_Flop t_ff_4 (.clk(t_ff_1_q[2]), .T(in_2), .Q(t_ff_1_q[3]), .preset(button_1_out));  // open: Qn, reset, en
  Hex_Digit_Display hex_digit_display_2 (.value(not_2_out));  // open: dp
  assign not_2_out = ~t_ff_1_q;  // NOT_Gate not_2, 4 bits wide

  // Notes on the sheet:
  //   Q_4)Contador Crescente
endmodule

module Flip_Flop_T (
  input  Clock,
  input  Entrada,
  output Q,
  output Q_prime
);

  wire and_1_out, and_2_out;

  and and_1 (and_1_out, Q, Entrada, Clock);
  and and_2 (and_2_out, Clock, Entrada, Q_prime);
  nor nor_1 (Q, and_1_out, Q_prime);
  nor nor_2 (Q_prime, Q, and_2_out);

  // Notes on the sheet:
  //   FLip Flop tipo T
endmodule
