// Logisim project t24.circ as structural Verilog: 6 circuits, main circuit main
module main (
  input  in_1,
  input  in_2,
  input  in_3,
  input  in_4,
  input  in_5
);

  wire button_1_out, clock_1_out, clock_2_out, clock_3_out, d_1_q1, d_ff_1_q, multiplexer_1_out,
       multiplexer_2_out;
  wire [3:0] not_1_out, t_ff_1_q;
  wire [7:0] undriven;

  Clock clock_1 (.out(clock_1_out));
  Button button_1 (.out(button_1_out));
  Multiplexer multiplexer_1 (.in0(d_ff_1_q), .in1(in_2), .out(multiplexer_1_out), .sel(in_4));  // open: en
  // NAND_Gate nand_1 has open pins: in0=in_1, in1=in_1, out=open
  Clock clock_2 (.out(clock_2_out));
  D_Flip_Flop d_ff_1 (.clk(clock_2_out), .D(multiplexer_1_out), .Q(d_ff_1_q));  // open: Qn, preset, en, reset
  T_Flip_Flop t_ff_1 (.clk(clock_1_out), .T(in_1), .Q(t_ff_1_q[0]), .preset(button_1_out));  // open: Qn, reset, en
  T_Flip_Flop t_ff_2 (.clk(t_ff_1_q[0]), .T(in_1), .Q(t_ff_1_q[1]), .preset(button_1_out));  // open: Qn, reset, en
  T_Flip_Flop t_ff_3 (.clk(t_ff_1_q[1]), .T(in_1), .Q(t_ff_1_q[2]), .preset(button_1_out));  // open: Qn, reset, en
  T_Flip_Flop t_ff_4 (.clk(t_ff_1_q[2]), .T(in_1), .Q(t_ff_1_q[3]), .preset(button_1_out));  // open: Qn, reset, en
  Multiplexer multiplexer_2 (.in0(d_1_q1), .in1(in_3), .out(multiplexer_2_out), .sel(in_5));  // open: en
  Clock clock_3 (.out(clock_3_out));
  D d_1 (.entreada(clock_3_out), .clock(multiplexer_2_out), .q1(d_1_q1));  // open: q2
  Hex_Digit_Display hex_digit_display_1 (.value(not_1_out));  // open: dp
  assign not_1_out = ~t_ff_1_q;  // NOT_Gate not_1, 4 bits wide
  Demultiplexer #(.select(3), .width(8)) demultiplexer_1 (.in(undriven));  // open: out0, out1, out2, out3, out4, out5, out6, out7, sel, en
  Decoder decoder_1 ();  // open: out0, out1, sel, en
endmodule

module D (
  input  entreada,
  input  clock,
  output q1,
  output q2
);

  wire nand_1_out, nand_2_out;

  nand nand_1 (nand_1_out, entreada, clock);
  nand nand_2 (nand_2_out, nand_1_out, clock);
  nand nand_3 (q1, nand_1_out, q2);
  nand nand_4 (q2, q1, nand_2_out);
endmodule

module Reg_8bits (
  input  in_1,
  input  in_2,
  input  in_3,
  input  [7:0] in_4,
  output [7:0] out_5
);

  wire clock_1_out, priority_encoder_1_en_out, priority_encoder_1_gs, serial_1_s, undriven, undriven_2;
  wire [2:0] priority_encoder_1_out;
  wire [7:0] demultiplexer_1_out1;

  Clock clock_1 (.out(clock_1_out));
  D_Flip_Flop d_ff_1 (.clk(in_3), .D(in_4[7]), .Q(out_5[7]));  // open: Qn, preset, en, reset
  serial serial_1 (.Entrada(in_1), .Clock(clock_1_out), .Clear(in_2), .S(serial_1_s));
  D_Flip_Flop d_ff_2 (.clk(in_3), .D(in_4[6]), .Q(out_5[6]));  // open: Qn, preset, en, reset
  D_Flip_Flop d_ff_3 (.clk(in_3), .D(in_4[5]), .Q(out_5[5]));  // open: Qn, preset, en, reset
  Demultiplexer #(.select(3), .width(8)) demultiplexer_1 (
    .out1(demultiplexer_1_out1), .in(in_4));  // open: out0, out2, out3, out4, out5, out6, out7, sel, en
  D_Flip_Flop d_ff_4 (.clk(in_3), .D(in_4[4]), .Q(out_5[4]));  // open: Qn, preset, en, reset
  Multiplexer multiplexer_1 (.sel(undriven), .en(undriven_2));  // open: in0, in1, out
  D_Flip_Flop d_ff_5 (.clk(in_3), .D(in_4[3]), .Q(out_5[3]));  // open: Qn, preset, en, reset
  Decoder #(.select(4)) decoder_1 ();  // open: out0, out1, out2, out3, out4, out5, out6, out7, out8, out9, out10, out11, out12, out13, out14, out15, sel, en
  D_Flip_Flop d_ff_6 (.clk(in_3), .D(in_4[2]), .Q(out_5[2]));  // open: Qn, preset, en, reset
  D_Flip_Flop d_ff_7 (.clk(in_3), .D(in_4[1]), .Q(out_5[1]));  // open: Qn, preset, en, reset
  Priority_Encoder priority_encoder_1 (
    .out(priority_encoder_1_out), .gs(priority_encoder_1_gs), .en_out(priority_encoder_1_en_out));  // open: in0, in1, in2, in3, in4, in5, in6, in7, en_in
  D_Flip_Flop d_ff_8 (.clk(in_3), .D(in_4[0]), .Q(out_5[0]));  // open: Qn, preset, en, reset
endmodule

module serial (
  input  Entrada,
  input  Clock,
  input  Clear,
  output S
);

  wire d_ff_1_q, d_ff_2_q, d_ff_3_q;

  D_Flip_Flop d_ff_1 (.clk(Clock), .D(Entrada), .Q(d_ff_1_q), .en(Clear));  // open: Qn, preset, reset
  D_Flip_Flop d_ff_2 (.clk(Clock), .D(d_ff_1_q), .Q(d_ff_2_q), .en(Clear));  // open: Qn, preset, reset
  D_Flip_Flop d_ff_3 (.clk(Clock), .D(d_ff_2_q), .Q(d_ff_3_q), .en(Clear));  // open: Qn, preset, reset
  D_Flip_Flop d_ff_4 (.clk(Clock), .D(d_ff_3_q), .Q(S), .en(Clear));  // open: Qn, preset, reset

  // Notes on the sheet:
  //   Serial
endmodule

module paralelo (
  input  in_1,
  input  [7:0] in_2,
  output [7:0] out_3
);

  D_Flip_Flop d_ff_1 (.clk(in_1), .D(in_2[7]), .Q(out_3[7]));  // open: Qn, preset, en, reset
  D_Flip_Flop d_ff_2 (.clk(in_1), .D(in_2[6]), .Q(out_3[6]));  // open: Qn, preset, en, reset
  D_Flip_Flop d_ff_3 (.clk(in_1), .D(in_2[5]), .Q(out_3[5]));  // open: Qn, preset, en, reset
  D_Flip_Flop d_ff_4 (.clk(in_1), .D(in_2[4]), .Q(out_3[4]));  // open: Qn, preset, en, reset
  D_Flip_Flop d_ff_5 (.clk(in_1), .D(in_2[3]), .Q(out_3[3]));  // open: Qn, preset, en, reset
  D_Flip_Flop d_ff_6 (.clk(in_1), .D(in_2[2]), .Q(out_3[2]));  // open: Qn, preset, en, reset
  D_Flip_Flop d_ff_7 (.clk(in_1), .D(in_2[1]), .Q(out_3[1]));  // open: Qn, preset, en, reset
  D_Flip_Flop d_ff_8 (.clk(in_1), .D(in_2[0]), .Q(out_3[0]));  // open: Qn, preset, en, reset

  // Notes on the sheet:
  //   Reg Paralelo
endmodule

module q5 (
  input  Load,
  input  Entrada_Serial,
  input  Paralelo_Serial,
  input  [7:0] Entrada_Paralelo,
  output [7:0] out_5
);

  wire clock_1_out, multiplexer_1_out, multiplexer_2_out, multiplexer_3_out, multiplexer_4_out,
       multiplexer_5_out, multiplexer_6_out, multiplexer_7_out, multiplexer_8_out, undriven;

  Clock clock_1 (.out(clock_1_out));
  D_Flip_Flop d_ff_1 (
    .clk(clock_1_out), .D(multiplexer_1_out), .Q(out_5[7]), .preset(Load), .reset(undriven));  // open: Qn, en
  Multiplexer multiplexer_1 (
    .in0(Entrada_Serial), .in1(Entrada_Paralelo[7]), .out(multiplexer_1_out), .sel(Paralelo_Serial));  // open: en
  D_Flip_Flop d_ff_2 (
    .clk(clock_1_out), .D(multiplexer_2_out), .Q(out_5[6]), .preset(Load), .reset(undriven));  // open: Qn, en
  Multiplexer multiplexer_2 (
    .in0(out_5[7]), .in1(Entrada_Paralelo[6]), .out(multiplexer_2_out), .sel(Paralelo_Serial));  // open: en
  D_Flip_Flop d_ff_3 (
    .clk(clock_1_out), .D(multiplexer_3_out), .Q(out_5[5]), .preset(Load), .reset(undriven));  // open: Qn, en
  Multiplexer multiplexer_3 (
    .in0(out_5[6]), .in1(Entrada_Paralelo[5]), .out(multiplexer_3_out), .sel(Paralelo_Serial));  // open: en
  D_Flip_Flop d_ff_4 (
    .clk(clock_1_out), .D(multiplexer_4_out), .Q(out_5[4]), .preset(Load), .reset(undriven));  // open: Qn, en
  Multiplexer multiplexer_4 (
    .in0(out_5[5]), .in1(Entrada_Paralelo[4]), .out(multiplexer_4_out), .sel(Paralelo_Serial));  // open: en
  D_Flip_Flop d_ff_5 (
    .clk(clock_1_out), .D(multiplexer_5_out), .Q(out_5[3]), .preset(Load), .reset(undriven));  // open: Qn, en
  Multiplexer multiplexer_5 (
    .in0(out_5[4]), .in1(Entrada_Paralelo[3]), .out(multiplexer_5_out), .sel(Paralelo_Serial));  // open: en
  D_Flip_Flop d_ff_6 (
    .clk(clock_1_out), .D(multiplexer_6_out), .Q(out_5[2]), .preset(Load), .reset(undriven));  // open: Qn, en
  Multiplexer multiplexer_6 (
    .in0(out_5[3]), .in1(Entrada_Paralelo[2]), .out(multiplexer_6_out), .sel(Paralelo_Serial));  // open: en
  D_Flip_Flop d_ff_7 (
    .clk(clock_1_out), .D(multiplexer_7_out), .Q(out_5[1]), .preset(Load), .reset(undriven));  // open: Qn, en
  Multiplexer multiplexer_7 (
    .in0(out_5[2]), .in1(Entrada_Paralelo[1]), .out(multiplexer_7_out), .sel(Paralelo_Serial));  // open: en
  D_Flip_Flop d_ff_8 (
    .clk(clock_1_out), .D(multiplexer_8_out), .Q(out_5[0]), .preset(Load), .reset(undriven));  // open: Qn, en
  Multiplexer multiplexer_8 (
    .in0(out_5[1]), .in1(Entrada_Paralelo[0]), .out(multiplexer_8_out), .sel(Paralelo_Serial));  // open: en

  // Notes on the sheet:
  //   Questão 5
endmodule
